# Fritzing sketch cakeExtruderSchematic (saved by Fritzing 0.9.3b)
breadboards: 1

parts:
  high_current_H-bridge_driver = A4950 [package=soicn]
  Part1 = Arduino Uno (Rev3) - ICSP
  M1 = DC Motor
  motor_position_pot = Rotary Potentiometer (Large) [maximum_resistance=10kΩ package=THT]
  ABB_24V_control_signal = AC Power [voltage=24 frequency=60]
  R1 = Resistor [tolerance=±5% resistance=6.2k package="0603 [SMD]"]
  R2 = Resistor [tolerance=±5% resistance=1.5k package="0603 [SMD]"]

nets:
  N1: high_current_H-bridge_driver.IN2, Part1.D5_PWM
  N2: high_current_H-bridge_driver.IN1, Part1.D6_PWM
  12V: high_current_H-bridge_driver.VBB
  N3: high_current_H-bridge_driver.OUT1, M1.pin_1
  N4: high_current_H-bridge_driver.OUT2, M1.pin_2
  N5: Part1.A0, motor_position_pot.wiper
  N6: Part1.5V, motor_position_pot.leg2
  N7: Part1.D8, R1.Pin_0, R2.Pin_1
  N8: Part1.GND, motor_position_pot.leg1
  N9: ABB_24V_control_signal.V-, R1.Pin_1
  GND: R2.Pin_0
